// Logisim project ALU.circ as structural Verilog: 1 circuit, main circuit ALU
module ALU (
  input  [31:0] A,
  input  [31:0] B,
  input  [4:0] Shift,
  input  [3:0] Codop,
  input  CarryIn,
  output [31:0] S,
  output [3:0] Flags
);

  wire adder_1_cout, adder_2_cout, subtractor_1_bout, subtractor_2_bout, subtractor_3_bout;
  wire [31:0] D, E, F, G, H, I, J, K, L, M, not_1_out, O, P, Q, R, S_t, subtractor_1_out, T;

  assign not_1_out = ~B;  // NOT_Gate not_1, 32 bits wide
  assign R = ~B;  // NOT_Gate not_2, 32 bits wide
  assign D = A ^ A;  // XOR_Gate xor_1, 32 bits wide
  Shifter #(.width(32)) shifter_1 (.in(B), .\dist (Shift), .out(E));
  Shifter #(.shift("lr"), .width(32)) shifter_2 (.in(B), .\dist (Shift), .out(F));
  Shifter #(.shift("ar"), .width(32)) shifter_3 (.in(B), .\dist (Shift), .out(G));
  Adder #(.width(32)) adder_1 (.a(A), .b(B), .out(H), .cin(CarryIn), .cout(adder_1_cout));
  Subtractor #(.width(32)) subtractor_1 (.a(A), .b(B), .out(subtractor_1_out), .bin(CarryIn), .bout(subtractor_1_bout));
  Shifter #(.shift("rr"), .width(32)) shifter_4 (.in(B), .\dist (Shift), .out(J));
  Subtractor #(.width(32)) subtractor_2 (.a({32{1'b0}}), .b(A), .out(L), .bout(subtractor_2_bout));  // open: bin
  Subtractor #(.width(32)) subtractor_3 (.a(A), .b(B), .out(M), .bout(subtractor_3_bout));  // open: bin
  Adder #(.width(32)) adder_2 (.a(A), .b(B), .out(T), .cout(adder_2_cout));  // open: cin
  Multiplier #(.width(32)) multiplier_1 (.a(A), .b(B), .out(P));  // open: cin, cout
  assign S_t = A & A;  // AND_Gate and_1, 32 bits wide
  assign K = A & B;  // AND_Gate and_2, 32 bits wide
  assign O = A | B;  // OR_Gate or_1, 32 bits wide
  assign Q = A & not_1_out;  // AND_Gate and_3, 32 bits wide
  Multiplexer #(.enable("false"), .select(4), .width(32)) multiplexer_1 (
    .in0(S_t), .in1(D), .in2(E), .in3(F), .in4(G), .in5(H), .in6(I), .in7(J), .in8(K), .in9(L), .in10(M),
    .in11(T), .in12(O), .in13(P), .in14(Q), .in15(R), .out(S), .sel(Codop));
  Subtractor #(.width(32)) subtractor_4 (.a(subtractor_1_out), .b(32'h1), .out(I));  // open: bin, bout
  Multiplexer #(.enable("false"), .select(4)) multiplexer_2 (
    .in0(1'b0), .in1(1'b0), .in2(1'b0), .in3(1'b0), .in4(1'b0), .in5(adder_1_cout), .in6(subtractor_1_bout),
    .in7(1'b0), .in8(1'b0), .in9(subtractor_2_bout), .in10(subtractor_3_bout), .in11(adder_2_cout),
    .in12(1'b0), .in13(1'b0), .in14(1'b0), .in15(1'b0), .out(Flags[2]), .sel(Codop));
  Multiplexer #(.enable("false"), .select(4)) multiplexer_3 (
    .in0(1'b0), .in1(1'b0), .in2(1'b0), .in3(1'b0), .in4(1'b0), .in5(adder_1_cout), .in6(subtractor_1_bout),
    .in7(1'b0), .in8(1'b0), .in9(1'b0), .in10(subtractor_3_bout), .in11(adder_2_cout), .in12(1'b0),
    .in13(1'b0), .in14(1'b0), .in15(1'b0), .out(Flags[3]), .sel(Codop));
  Comparator #(.width(32)) comparator_1 (.a(S), .b({32{1'b0}}), .eq(Flags[1]), .lt(Flags[0]));  // open: gt

  // Other names for the same wires on the sheet: Cin = CarryIn; COp[3:0] = Codop; N = Flags[0]; Z = Flags[1];
  //   C = Flags[2]; V = Flags[3]

  // Notes on the sheet:
  //   Note: for ROR, C = N
  //   Note 2: assume that shift > 0 for LSL and LSR
endmodule
