// Logisim project Ctl_Data_Processing.circ as structural Verilog: 1 circuit, main circuit Data_Processing
module Data_Processing (
  input  Enable,
  input  [15:0] Instruction,
  output [2:0] Rd,
  output [2:0] Rn,
  output [2:0] Rm,
  output [3:0] ALU_Opcode,
  output [3:0] Flags_Update_Mask
);

  wire c, n_t, v, z;
  wire [2:0] and_1_out, D, M, multiplexer_2_out, N, undriven, xor_1_out;

  assign and_1_out = D & M;  // AND_Gate and_1, 3 bits wide
  assign xor_1_out = D ^ M;  // XOR_Gate xor_1, 3 bits wide
  Shifter #(.width(3)) shifter_1 (.in(D));  // open: dist, out
  assign Rd = Enable ? D : 3'bz;  // Controlled_Buffer controlled_buffer_1
  assign Rn = Enable ? N : 3'bz;  // Controlled_Buffer controlled_buffer_2
  assign Rm = Enable ? M : 3'bz;  // Controlled_Buffer controlled_buffer_3
  assign ALU_Opcode = Enable ? Instruction[9:6] : 4'bz;  // Controlled_Buffer controlled_buffer_4
  assign Flags_Update_Mask = Enable ? {v, c, z, n_t} : 4'bz;  // Controlled_Buffer controlled_buffer_5
  Multiplexer #(.enable("false"), .select(4), .width(3)) multiplexer_1 (
    .in0(Instruction[2:0]), .in1(Instruction[2:0]), .in2(Instruction[2:0]), .in3(Instruction[2:0]),
    .in4(Instruction[2:0]), .in5(Instruction[2:0]), .in6(Instruction[2:0]), .in7(Instruction[2:0]),
    .in8(3'b000), .in9(Instruction[2:0]), .in10(3'b000), .in11(3'b000), .in12(Instruction[2:0]),
    .in13(Instruction[2:0]), .in14(Instruction[2:0]), .in15(Instruction[2:0]), .out(D), .sel(Instruction[9:6]));
  Pull_Resistor pull_resistor_1 (.node(Rd));
  Pull_Resistor pull_resistor_2 (.node(Rn));
  Pull_Resistor pull_resistor_3 (.node(Rm));
  Pull_Resistor pull_resistor_4 (.node(ALU_Opcode));
  Pull_Resistor pull_resistor_5 (.node(Flags_Update_Mask));
  Multiplexer #(.enable("false"), .select(4), .width(3)) multiplexer_2 (
    .in0(and_1_out), .in1(xor_1_out), .in2(undriven), .out(multiplexer_2_out), .sel(Instruction[9:6]));  // open: in3, in4, in5, in6, in7, in8, in9, in10, in11, in12, in13, in14, in15
  Comparator #(.width(3)) comparator_1 (.a(multiplexer_2_out), .b(3'b000), .eq(z), .lt(n_t));  // open: gt
  Multiplexer #(.enable("false"), .select(4), .width(3)) multiplexer_3 (
    .in0(Instruction[5:3]), .in1(Instruction[5:3]), .in2(Instruction[5:3]), .in3(Instruction[5:3]),
    .in4(Instruction[5:3]), .in5(Instruction[5:3]), .in6(Instruction[5:3]), .in7(Instruction[5:3]),
    .in8(Instruction[5:3]), .in9(3'b000), .in10(Instruction[5:3]), .in11(Instruction[5:3]),
    .in12(Instruction[5:3]), .in13(Instruction[2:0]), .in14(Instruction[5:3]), .in15(Instruction[5:3]),
    .out(M), .sel(Instruction[9:6]));
  Multiplexer #(.enable("false"), .select(4), .width(3)) multiplexer_4 (
    .in0(Instruction[2:0]), .in1(Instruction[2:0]), .in2(Instruction[2:0]), .in3(Instruction[2:0]),
    .in4(Instruction[2:0]), .in5(Instruction[2:0]), .in6(Instruction[2:0]), .in7(Instruction[2:0]),
    .in8(Instruction[2:0]), .in9(Instruction[5:3]), .in10(Instruction[2:0]), .in11(Instruction[2:0]),
    .in12(Instruction[2:0]), .in13(Instruction[5:3]), .in14(Instruction[2:0]), .in15(3'b000), .out(N),
    .sel(Instruction[9:6]));

  // Other names for the same wires on the sheet: Alu[3:0] = Instruction[9:6]; I[15:0] = Instruction;
  //   threeFourFive[2:0] = Instruction[5:3]; zeroOneTwo[2:0] = Instruction[2:0]

  // Notes on the sheet:
  //   Note 2: RSB instruction has Rn as 1st operand.
  //   MUL instruction has Rn as 1st operand and Rdm as 2nd operand
  //   For simplification purposes, Rm is used for 1st operand both here and in the ALU.
  //   Note: instructions that does not save the result will still have the second operand as the destination register, the ALU will copy the second register to the destination register
  //   Pull output low on Enable = 0
endmodule
