// Logisim project Ctl_Flags_APSR.circ as structural Verilog: 1 circuit, main circuit Flags_APSR
module Flags_APSR (
  input  [3:0] Update_Mask,
  input  [3:0] Flags_In,
  input  Rst,
  input  Clk,
  output [3:0] Flags_Out
);

  wire [3:0] and_1_out, and_2_out, not_1_out, or_1_out;

  assign not_1_out = ~Update_Mask;  // NOT_Gate not_1, 4 bits wide
  assign and_1_out = Update_Mask & Flags_In;  // AND_Gate and_1, 4 bits wide
  assign and_2_out = not_1_out & Flags_Out;  // AND_Gate and_2, 4 bits wide
  assign or_1_out = and_1_out | and_2_out;  // OR_Gate or_1, 4 bits wide
  Register #(.width(4)) register_1 (.D(or_1_out), .en(1'b1), .clk(Rst), .Q(Flags_Out), .clr(Clk));

  // Other names for the same wires on the sheet: FLout[3:0] = Flags_Out
endmodule
