// Logisim project Ctl_Load_Store.circ as structural Verilog: 1 circuit, main circuit Load_Store
module Load_Store (
  input  [15:0] Instruction,
  input  Enable,
  input  Clk,
  input  Reset,
  input  [31:0] Stack_Pointer,
  input  in_6,
  input  in_7,
  output Store,
  output Load,
  output PC_Hold,
  output [2:0] Rmd,
  output [31:0] RAM_Addr
);

  wire [31:0] bit_extender_1_out;

  Comparator #(.width(4)) comparator_1 (.a(Instruction[15:12]), .b(4'b1001), .eq(in_7));  // open: gt, lt
  assign bit_extender_1_out = {{24{Instruction[7]}}, Instruction[7:0]};  // Bit_Extender bit_extender_1
  Comparator #(.width(1)) comparator_2 (.a(Instruction[11]), .b(1'b0), .gt(PC_Hold), .eq(Store));  // open: lt
  Adder #(.width(32)) adder_1 (.a(bit_extender_1_out), .b(Stack_Pointer), .out(RAM_Addr));  // open: cin, cout
  D_Flip_Flop d_ff_1 (.D(PC_Hold), .clk(Clk), .Q(Load), .reset(Reset));  // open: Qn, preset
  Comparator #(.width(1)) comparator_3 (.a(in_6), .b(1'b0));  // open: gt, eq, lt

  // Other names for the same wires on the sheet: Ins[15:0] = Instruction; imm8[7:0] = Instruction[7:0]; Rst = Reset;
  //   Rt[2:0] = Instruction[10:8]; SP[31:0] = Stack_Pointer

  // Notes on the sheet:
  //   Instruction: pull=down
  //   Delay load and hold PC for 1 cycle for the RAM to send out requested data 
endmodule
