// Logisim project Ctl_SP_Address.circ as structural Verilog: 1 circuit, main circuit SP_Address
module SP_Address (
  input  [31:0] Stack_Pointer,
  input  [15:0] Instruction,
  input  Enable,
  output [31:0] New_Stack_Pointer,
  output Write_Enable
);

  wire comparator_1_eq, comparator_1_gt, not_1_out;
  wire [15:0] controlled_buffer_1_out, controlled_buffer_2_out;
  wire [31:0] bit_extender_1_out, bit_extender_2_out;

  Comparator #(.width(1)) comparator_1 (
    .a(Instruction[6]), .b(1'b0), .gt(comparator_1_gt), .eq(comparator_1_eq));  // open: lt
  assign controlled_buffer_1_out = comparator_1_gt ? Instruction : 16'bz;  // Controlled_Buffer controlled_buffer_1
  assign controlled_buffer_2_out = not_1_out ? Instruction : 16'bz;  // Controlled_Buffer controlled_buffer_2
  not not_1 (not_1_out, comparator_1_eq);
  Comparator #(.width(1)) comparator_2 (.a(Enable), .b(1'b1), .eq(Write_Enable));  // open: gt, lt
  assign bit_extender_1_out = {{25{1'b0}}, controlled_buffer_1_out[6:0]};  // Bit_Extender bit_extender_1
  assign bit_extender_2_out = {{25{1'b0}}, controlled_buffer_2_out[6:0]};  // Bit_Extender bit_extender_2
  Adder #(.width(32)) adder_1 (.a(Stack_Pointer), .b(bit_extender_1_out), .out(New_Stack_Pointer));  // open: cin, cout
  Subtractor #(.width(32)) subtractor_1 (
    .a(Stack_Pointer), .b(bit_extender_2_out), .out(New_Stack_Pointer));  // open: bin, bout

  // Other names for the same wires on the sheet: NewSP[31:0] = New_Stack_Pointer; SP[31:0] = Stack_Pointer

  // Notes on the sheet:
  //   Pull output low on Enable = 0
endmodule
