// Logisim project Ctl_Shift_Add_Sub_Mov.circ as structural Verilog: 10 circuits, main circuit Shift_Add_Sub_Mov
module Shift_Add_Sub_Mov (
  input  Enable,
  input  [15:0] Instruction,
  output [3:0] Flags_Update_Mask,
  output Carry,
  output imm32_enabled,
  output [2:0] Rm,
  output [2:0] Rn,
  output [2:0] Rd,
  output [4:0] Imm5,
  output [31:0] Imm32,
  output [3:0] ALU_Opcode
);

  wire and_2_out, and_4_out, comparator_1_eq, comparator_2_eq, imm5_enable_1_imm5_enabled,
       imm32_enable_1_enabled, rn_out_1_rn_out_nb;
  wire [1:0] enabled_logic_1_v_out, enabled_logic_2_v_out, enabled_logic_3_v_out, imm32_out_1_imm32_out_nb,
       rd_out_1_rd_out_nb, rm_out_1_rm_out_nb;
  wire [3:0] ALU_Opcode_t, flags_1_flags_out;
  wire [31:0] bit_extender_1_out, bit_extender_2_out, multiplexer_3_out, negator_1_out;

  Comparator #(.width(4)) comparator_1 (.a(ALU_Opcode_t), .b(4'b0110), .eq(comparator_1_eq));  // open: gt, lt
  assign bit_extender_1_out = {{29{1'b0}}, Instruction[8:6]};  // Bit_Extender bit_extender_1
  and and_1 (Carry, comparator_1_eq, Enable);
  assign bit_extender_2_out = {{24{1'b0}}, Instruction[7:0]};  // Bit_Extender bit_extender_2
  opcode opcode_1 (.opcode(Instruction[13:9]), .codop(ALU_Opcode_t));
  imm32_enable imm32_enable_1 (.opcode(Instruction[13:9]), .enabled(imm32_enable_1_enabled));
  Multiplexer #(.enable("false"), .width(4)) multiplexer_1 (
    .in0(4'b0000), .in1(flags_1_flags_out), .out(Flags_Update_Mask), .sel(Enable));
  flags flags_1 (.codeop(ALU_Opcode_t), .flags_out(flags_1_flags_out));
  Multiplexer #(.enable("false"), .width(5)) multiplexer_2 (
    .in0({5{1'b0}}), .in1(Instruction[10:6]), .out(Imm5), .sel(and_2_out));
  and and_2 (and_2_out, imm5_enable_1_imm5_enabled, Enable);
  imm5_enable imm5_enable_1 (.opcode(ALU_Opcode_t), .imm5_enabled(imm5_enable_1_imm5_enabled));
  rm_out rm_out_1 (.opcode(Instruction[13:9]), .rm_out_nb(rm_out_1_rm_out_nb));
  rd_out rd_out_1 (.opcode(Instruction[13:9]), .rd_out_nb(rd_out_1_rd_out_nb));
  imm32_out imm32_out_1 (.opcode(Instruction[13:9]), .imm32_out_nb(imm32_out_1_imm32_out_nb));
  and and_3 (imm32_enabled, imm32_enable_1_enabled, Enable);
  Comparator #(.width(2)) comparator_2 (.a(Instruction[12:11]), .b(2'b00), .eq(comparator_2_eq));  // open: gt, lt
  Negator #(.width(32)) negator_1 (.in(bit_extender_2_out), .out(negator_1_out));
  enabled_logic enabled_logic_1 (.v_in(rm_out_1_rm_out_nb), .enable(Enable), .v_out(enabled_logic_1_v_out));
  enabled_logic enabled_logic_2 (.v_in(rd_out_1_rd_out_nb), .enable(Enable), .v_out(enabled_logic_2_v_out));
  Multiplexer #(.enable("false"), .width(32)) multiplexer_3 (
    .in0(bit_extender_2_out), .in1(negator_1_out), .out(multiplexer_3_out), .sel(comparator_2_eq));
  Multiplexer #(.enable("false"), .width(4)) multiplexer_4 (
    .in0(4'b0000), .in1(ALU_Opcode_t), .out(ALU_Opcode), .sel(Enable));
  Multiplexer #(.enable("false"), .select(2), .width(3)) multiplexer_5 (
    .in0(3'b000), .in1(Instruction[5:3]), .in2(Instruction[8:6]), .out(Rm), .sel(enabled_logic_1_v_out));  // open: in3
  Multiplexer #(.enable("false"), .select(2), .width(3)) multiplexer_6 (
    .in0(3'b000), .in1(Instruction[2:0]), .in2(Instruction[10:8]), .out(Rd), .sel(enabled_logic_2_v_out));  // open: in3
  Multiplexer #(.enable("false"), .select(2), .width(32)) multiplexer_7 (
    .in0({32{1'b0}}), .in1(bit_extender_1_out), .in2(multiplexer_3_out), .out(Imm32),
    .sel(enabled_logic_3_v_out));  // open: in3
  enabled_logic enabled_logic_3 (.v_in(imm32_out_1_imm32_out_nb), .enable(Enable), .v_out(enabled_logic_3_v_out));
  and and_4 (and_4_out, rn_out_1_rn_out_nb, Enable);
  rn_out rn_out_1 (.opcode(Instruction[13:9]), .rn_out_nb(rn_out_1_rn_out_nb));
  Multiplexer #(.enable("false"), .width(3)) multiplexer_8 (
    .in0(3'b000), .in1(Instruction[5:3]), .out(Rn), .sel(and_4_out));

  // Other names for the same wires on the sheet: carry_enabled = Carry; en = Enable;
  //   flags_update[3:0] = Flags_Update_Mask; Instru[15:0] = Instruction

  // Notes on the sheet:
  //   Note: ALU uses Rn register for shifts. Use Rn instead of Rm for shifts (immediate) here too
  //   Note 3: Imm32_Enable forces the use of the immediate for Rm register
  //   Note 2: MOV uses RSB ALU opcode with Imm8 reversed so that it is copied to output register
  //   Pull output low on Enable = 0
  //   only ADD and SUB use Rm
  //   Enable carry for SUB since it is reversed in ALU
  //   ALU will use Imm32 instead of Rm
endmodule

module opcode (
  input  [4:0] opcode,
  output [3:0] codop
);

  wire and_2_out, and_3_out, and_4_out, and_5_out, and_6_out, and_7_out, not_1_out, not_2_out, not_3_out,
       not_4_out;

  not not_1 (not_1_out, opcode[4]);
  not not_2 (not_2_out, opcode[3]);
  not not_3 (not_3_out, opcode[2]);
  not not_4 (not_4_out, opcode[0]);
  and and_1 (codop[3], opcode[4], not_2_out);
  and and_2 (and_2_out, not_1_out, not_2_out);
  and and_3 (and_3_out, opcode[2], opcode[0]);
  or or_1 (codop[1], and_2_out, and_3_out, and_4_out);
  and and_4 (and_4_out, opcode[4], opcode[2]);
  and and_5 (and_5_out, not_1_out, not_2_out, opcode[2]);
  and and_6 (and_6_out, not_1_out, opcode[2], not_4_out);
  or or_2 (codop[0], and_5_out, and_6_out, and_7_out);
  and and_7 (and_7_out, opcode[4], not_3_out);

  assign codop[2] = opcode[3];
endmodule

module imm32_enable (
  input  [4:0] opcode,
  output enabled
);

  wire and_1_out;

  and and_1 (and_1_out, opcode[3], opcode[2], opcode[1]);
  or or_1 (enabled, and_1_out, opcode[4]);
endmodule

module imm5_enable (
  input  [3:0] opcode,
  output imm5_enabled
);

  wire and_1_out, and_2_out, not_1_out, not_2_out, not_3_out, not_4_out;

  not not_1 (not_1_out, opcode[3]);
  not not_2 (not_2_out, opcode[2]);
  not not_3 (not_3_out, opcode[1]);
  not not_4 (not_4_out, opcode[0]);
  and and_1 (and_1_out, not_1_out, not_2_out, opcode[1]);
  and and_2 (and_2_out, not_1_out, opcode[2], not_3_out, not_4_out);
  or or_1 (imm5_enabled, and_1_out, and_2_out);
endmodule

module rm_out (
  input  [4:0] opcode,
  output [1:0] rm_out_nb
);

  wire and_2_out, and_3_out, not_1_out, not_2_out, not_3_out, not_4_out;

  not not_1 (not_1_out, opcode[4]);
  not not_2 (not_2_out, opcode[3]);
  not not_3 (not_3_out, opcode[2]);
  not not_4 (not_4_out, opcode[1]);
  and and_1 (rm_out_nb[1], not_1_out, opcode[3], opcode[2], not_4_out);
  and and_2 (and_2_out, not_1_out, not_2_out);
  or or_1 (rm_out_nb[0], and_2_out, and_3_out);
  and and_3 (and_3_out, not_1_out, not_3_out);
endmodule

module rn_out (
  input  [4:0] opcode,
  output rn_out_nb
);

  wire not_1_out;

  not not_1 (not_1_out, opcode[4]);
  and and_1 (rn_out_nb, not_1_out, opcode[3], opcode[2]);
endmodule

module rd_out (
  input  [4:0] opcode,
  output [1:0] rd_out_nb
);

  not not_1 (rd_out_nb[0], opcode[4]);

  assign rd_out_nb[1] = opcode[4];
endmodule

module imm32_out (
  input  [4:0] opcode,
  output [1:0] imm32_out_nb
);

  wire not_1_out;

  not not_1 (not_1_out, opcode[4]);
  and and_1 (imm32_out_nb[0], not_1_out, opcode[3], opcode[2], opcode[1]);

  assign imm32_out_nb[1] = opcode[4];
endmodule

module enabled_logic (
  input  [1:0] v_in,
  input  enable,
  output [1:0] v_out
);

  and and_1 (v_out[1], v_in[1], enable);
  and and_2 (v_out[0], v_in[0], enable);
endmodule

module flags (
  input  [3:0] codeop,
  output [3:0] flags_out
);

  wire and_1_out, and_2_out, and_3_out, and_4_out, and_5_out, and_6_out, and_7_out, and_8_out, and_9_out,
       and_10_out, and_11_out, and_12_out, and_13_out, and_14_out, and_15_out, and_16_out, and_17_out,
       not_1_out, not_2_out, not_3_out, not_4_out;

  not not_1 (not_1_out, codeop[3]);
  not not_2 (not_2_out, codeop[2]);
  not not_3 (not_3_out, codeop[1]);
  not not_4 (not_4_out, codeop[0]);
  and and_1 (and_1_out, not_1_out, not_2_out, codeop[1]);
  and and_2 (and_2_out, not_2_out, codeop[1], not_4_out);
  and and_3 (and_3_out, not_1_out, codeop[2], not_3_out);
  and and_4 (and_4_out, not_1_out, codeop[2], not_4_out);
  and and_5 (and_5_out, codeop[3], not_2_out, not_3_out, codeop[0]);
  and and_6 (and_6_out, not_1_out, not_2_out, codeop[1]);
  and and_7 (and_7_out, not_2_out, codeop[1], not_4_out);
  and and_8 (and_8_out, not_1_out, codeop[2], not_3_out);
  and and_9 (and_9_out, not_1_out, codeop[2], not_4_out);
  and and_10 (and_10_out, codeop[3], not_2_out, not_3_out, codeop[0]);
  and and_11 (and_11_out, not_1_out, not_2_out, codeop[1]);
  and and_12 (and_12_out, not_2_out, codeop[1], not_4_out);
  and and_13 (and_13_out, not_1_out, codeop[2], not_3_out);
  and and_14 (and_14_out, not_1_out, codeop[2], not_4_out);
  and and_15 (and_15_out, not_1_out, codeop[2], not_3_out, codeop[0]);
  and and_16 (and_16_out, not_1_out, codeop[2], codeop[1], not_4_out);
  and and_17 (and_17_out, codeop[3], not_2_out, codeop[1], not_4_out);
  or or_1 (flags_out[3], and_1_out, and_2_out, and_3_out, and_4_out, and_5_out);
  or or_2 (flags_out[2], and_6_out, and_7_out, and_8_out, and_9_out, and_10_out);
  or or_3 (flags_out[1], and_11_out, and_12_out, and_13_out, and_14_out);
  or or_4 (flags_out[0], and_15_out, and_16_out, and_17_out);
endmodule
